# Fritzing sketch getTempContinuously (saved by Fritzing 0.9.3b)
breadboards: 1

parts:
  Raspberry_Pi_1 = Raspberry Pi 3 [part_number=RPI-3-V1.2]
  R3 = Resistor [tolerance=±5% resistance=10k package=THT]
  DHT1 = DHT22 Humidity and Temperature Sensor

nets:
  3V3: Raspberry_Pi_1.3v3, R3.Pin_0, DHT1.VDD
  N1: Raspberry_Pi_1.GPIO4, R3.Pin_1, DHT1.DATA
  GND: Raspberry_Pi_1.GND, DHT1.GND
