# Fritzing sketch getTempContinuouslyWaterSensor (saved by Fritzing 0.9.3b)
breadboards: 1

parts:
  Raspberry_Pi_1 = Raspberry Pi 3 [part_number=RPI-3-V1.2]
  R3 = Resistor [tolerance=±5% resistance=10k package=THT]
  DS1 = DS18B20 1-Wire Temperature Sensor Probe Cable
  R4 = Resistor [tolerance=±5% resistance=10k package=THT]

nets:
  3V3: Raspberry_Pi_1.3v3, R3.Pin_0, DS1.VDD, R4.Pin_0
  N1: Raspberry_Pi_1.GPIO4, R3.Pin_1, DS1.DQ, R4.Pin_1
  GND: Raspberry_Pi_1.GND, DS1.GND
