# Fritzing sketch getTempOnButtonPressWaterSensor (saved by Fritzing 0.9.3b)
breadboards: 1

parts:
  Raspberry_Pi_1 = Raspberry Pi 3 [part_number=RPI-3-V1.2]
  R2 = Resistor [tolerance=±5% resistance=10k package=THT]
  R3 = Resistor [tolerance=±5% resistance=10k package=THT]
  S1 = Pushbutton [package="[THT]"]
  DS1 = DS18B20 1-Wire Temperature Sensor Probe Cable
  LED1 = LED - 5mm [color="Green (560nm)" package="5 mm [THT]"]
  R1 = Resistor [tolerance=±5% resistance=220 package=THT]

nets (from the breadboard view):
  3V3: Raspberry_Pi_1.3v3, R2.Pin_1, R3.Pin_0, DS1.VDD, R1.Pin_1
  N1: Raspberry_Pi_1.GPIO4, R3.Pin_1, DS1.DQ
  N2: Raspberry_Pi_1.GPIO17, LED1.cathode
  N3: Raspberry_Pi_1.GPIO6, R2.Pin_0, S1.Pin_1, S1.Pin_2
  GND: Raspberry_Pi_1.GND, S1.Pin_3, S1.Pin_4, DS1.GND
  N4: LED1.anode, R1.Pin_0
