# Fritzing sketch getTempOnButtonPress (saved by Fritzing 0.9.3b)
breadboards: 1

parts:
  Raspberry_Pi_1 = Raspberry Pi 3 [part_number=RPI-3-V1.2]
  R1 = Resistor [tolerance=±5% resistance=220 package=THT]
  LED1 = LED - 5mm [color="Green (560nm)" package="5 mm [THT]"]
  R2 = Resistor [tolerance=±5% resistance=10k package=THT]
  R3 = Resistor [tolerance=±5% resistance=10k package=THT]
  DHT1 = DHT22 Humidity and Temperature Sensor
  S1 = Pushbutton [package="[THT]"]

nets (from the breadboard view):
  N1: Raspberry_Pi_1.3v3, R1.Pin_1, R2.Pin_1
  N2: Raspberry_Pi_1.GPIO4, R3.Pin_1, DHT1.DATA
  N3: Raspberry_Pi_1.GPIO17, LED1.cathode
  N4: Raspberry_Pi_1.GPIO6, R2.Pin_0, S1.Pin_1, S1.Pin_2
  GND: Raspberry_Pi_1.GND, DHT1.GND, S1.Pin_3, S1.Pin_4
  N5: R1.Pin_0, LED1.anode
  N6: R3.Pin_0, DHT1.VDD
